// Digital circuit p01 diagrams.dig as structural Verilog
module p01_diagrams (
  input  in_1,
  input  in_3,
  input  in_4,
  output out_2,
  output out_5
);

  wire nand_2_out;

  nand nand_1 (out_2, in_1, in_1);
  nand nand_2 (nand_2_out, in_3, in_4);
  nand nand_3 (out_5, nand_2_out, nand_2_out);

  // Notes on the sheet:
  //   Not Gate
  //   And Gate
endmodule
